# Fritzing sketch VADD_v2.0 (saved by Fritzing 1.0.6)
breadboards: 1

parts:
  Teensy1 = PJRC-TEENSY36-BASIC
  R1 = Rotary Potentiometer (Small) [maximum_resistance=10kΩ knob_status=50% power=0.5W package=THT]
  Part1 = Mono 2.5W Class D Audio Amplifier - PAM8302
  R2 = Rotary Potentiometer (Small) [maximum_resistance=10kΩ knob_status=50% power=0.5W package=THT]
  R3 = Rotary Potentiometer (Small) [maximum_resistance=10kΩ knob_status=50% power=0.5W package=THT]

nets:
  N1: Teensy1.connector46, R1.wiper
  N2: Teensy1.connector47, R3.wiper
  N3: Teensy1.connector48, R2.wiper
  N4: Teensy1.connector51, Part1.AIN+
  N5: Teensy1.connector55, R1.leg1, R2.leg1, R3.leg1
  N6: Teensy1.connector56, R1.leg2, R2.leg2, R3.leg2

custom parts:
  Mono 2.5W Class D Audio Amplifier - PAM8302: A super small but powerful mono amplifier able to deliver up to 2.5 Watts into 4-8 ohm impedance speakers. Inside the miniature chip is a class D controller, able to run from 2.0V-5.5VDC. Since the amp is a class D, its very efficient (over 90% efficient when driving an 8Ω speaker at over half a Watt) - making it perfect for portable and battery-powered projects.
